# Fritzing sketch File Rancangan Fritzing (saved by Fritzing 0.9.3b)
breadboards: 1

parts:
  U1 = ESP8266 NodeMCU LoLin module
  Part1 = RFID-RC522 [part_number=101218]
  J1 = Piezo Speaker
  S1 = Pushbutton [package="[SMD]"]
  R1 = Resistor [tolerance=±5% resistance=220 package=THT]
  R2 = Resistor [tolerance=±5% resistance=220 package=THT]
  LED1 = LED - 5mm [color="Red (633nm)" package="5 mm [THT]"]

nets:
  N1: U1.D1, J1.pin1
  N2: U1.D2, S1.Pin_1, S1.Pin_2, R1.Pin_1
  N3: U1.D3, Part1.RST
  N4: U1.D4, Part1.SDA
  3V3: U1.3V3, Part1.3.3V, S1.Pin_3, S1.Pin_4
  N5: U1.D5, Part1.SCK
  N6: U1.D6, Part1.MISO
  N7: U1.D7, Part1.MOSI
  N8: U1.D8, R2.Pin_1
  GND: U1.GND, Part1.GND, J1.pin2, R1.Pin_0, LED1.cathode
  N9: R2.Pin_0, LED1.anode

custom parts:
  ESP8266 NodeMCU LoLin module: ESP8266 based NodeMCU
